// Logisim project cpu.circ as structural Verilog: 1 circuit, main circuit cpu
module cpu (
  input  clk,
  input  [31:0] Instruction,
  input  [31:0] MemReadData,
  output [31:0] MemAddress,
  output [31:0] ProgramCounter,
  output [31:0] ra,
  output [31:0] sp,
  output [31:0] t0,
  output [31:0] t1,
  output [31:0] t2,
  output [31:0] s0,
  output [31:0] s1,
  output [31:0] a0,
  output [3:0] MemWriteMask,
  output [31:0] MemWriteData
);

  wire ASel, BrEq, BrLt, BrUn, control_logic_1_bsel, control_logic_1_regwen, MemWrite, PCSel;
  wire [1:0] control_logic_1_wbsel;
  wire [2:0] control_logic_1_immsel;
  wire [3:0] control_logic_1_alusel;
  wire [31:0] DataToReg, imm_gen_1_immediate, multiplexer_1_out, multiplexer_2_out, multiplexer_3_out,
       PCadd4, ReadData1, ReadData2, WriteData;

  Adder #(.width(32)) adder_1 (.a(ProgramCounter), .b(32'h4), .out(PCadd4));  // open: cin, cout
  Multiplexer #(.width(32)) multiplexer_1 (.in0(PCadd4), .in1(MemAddress), .out(multiplexer_1_out), .sel(PCSel));
  Register #(.width(32)) PC (.D(multiplexer_1_out), .clk(clk), .Q(ProgramCounter));  // open: en, clr
  branch_comp branch_comp_1 (.BrData1(ReadData1), .BrData2(ReadData2), .BrUn(BrUn), .BrEq(BrEq), .BrLt(BrLt));
  control_logic control_logic_1 (
    .Instruction(Instruction), .BrEq(BrEq), .BrLt(BrLt), .PCSel(PCSel), .RegWEn(control_logic_1_regwen),
    .ImmSel(control_logic_1_immsel), .BrUn(BrUn), .ASel(ASel), .BSel(control_logic_1_bsel),
    .ALUSel(control_logic_1_alusel), .MemWEn(MemWrite), .WBSel(control_logic_1_wbsel));
  regfile regfile_1 (
    .ReadIndex1(Instruction[19:15]), .ReadIndex2(Instruction[24:20]), .WriteIndex(Instruction[11:7]),
    .WriteData(WriteData), .RegWEn(control_logic_1_regwen), .clk(clk), .ra(ra), .sp(sp), .t0(t0), .t1(t1),
    .t2(t2), .s0(s0), .s1(s1), .a0(a0), .ReadData1(ReadData1), .ReadData2(ReadData2));
  imm_gen imm_gen_1 (.Instruction(Instruction), .ImmSel(control_logic_1_immsel), .Immediate(imm_gen_1_immediate));
  partial_store partial_store_1 (
    .Instruction(Instruction), .MemAddress(MemAddress), .DataFromReg(ReadData2), .MemWEn(MemWrite),
    .MemWriteMask(MemWriteMask), .DataToMem(MemWriteData));
  partial_load partial_load_1 (
    .Instruction(Instruction), .MemAddress(MemAddress), .DataFromMem(MemReadData), .DataToReg(DataToReg));
  Multiplexer #(.width(32)) multiplexer_2 (.in0(ReadData1), .in1(ProgramCounter), .out(multiplexer_2_out), .sel(ASel));
  Multiplexer #(.width(32)) multiplexer_3 (
    .in0(ReadData2), .in1(imm_gen_1_immediate), .out(multiplexer_3_out), .sel(control_logic_1_bsel));
  alu alu_1 (.A(multiplexer_2_out), .B(multiplexer_3_out), .ALUSel(control_logic_1_alusel), .ALUResult(MemAddress));
  Multiplexer #(.select(2), .width(32)) multiplexer_4 (
    .in0(DataToReg), .in1(MemAddress), .in2(PCadd4), .out(WriteData), .sel(control_logic_1_wbsel));  // open: in3

  // Other names for the same wires on the sheet: ALURes[31:0] = MemAddress; Rd[4:0] = Instruction[11:7];
  //   Rs1[4:0] = Instruction[19:15]; Rs2[4:0] = Instruction[24:20]

  // Notes on the sheet:
  //   To IMEM
  //   IMEM (do **NOT** move this)
  //   From IMEM
  //   Inputs/Outputs for testing. Do **NOT** move these.
  //   It is OK to move the PC, RegFile, ALU, MEM, Branch Comp, Imm Gen, Partial Load, Partial Store and Control Logic to wherever is most convenient for you when constructing your CPU, and to delete this text
  //   To DMEM
  //   DMEM (do **NOT** move this)
  //   From DMEM
endmodule
